# Fritzing sketch 12ch-hc-node-i2c (saved by Fritzing 0.9.3b)
circuit board: 9.9cm x 8.4cm
breadboards: 1

parts:
  RelayController-rev3 = Arduino Nano (Rev3.0)
  I2C = female pin header, 3 pins [form="♀ (female)"]
  Q1 = Basic FET P-Channel [package="TO220 [THT]"]
  Q2 = Basic FET P-Channel [package="TO220 [THT]"]
  J15 = female pin header, 3 pins [form="♀ (female)"]
  J16 = female pin header, 3 pins [form="♀ (female)"]
  DIMMER = screw terminal, 4 pins
  Q3 = NPN-Transistor [package="TO92 [THT]"]
  R1 = Resistor [tolerance=±5% resistance=10k package=THT]
  D1 = Rectifier Diode [part_number=1N4001 package="300 mil [THT]"]
  Q4 = NPN-Transistor [package="TO92 [THT]"]
  R2 = Resistor [tolerance=±5% resistance=220 package=THT]
  R3 = Resistor [tolerance=±5% resistance=220 package=THT]
  R4 = Resistor [tolerance=±5% resistance=220 package=THT]
  Q5 = NPN-Transistor [package="TO92 [THT]"]
  Q6 = NPN-Transistor [package="TO92 [THT]"]
  D3 = Rectifier Diode [part_number=1N4001 package="300 mil [THT]"]
  D4 = Rectifier Diode [part_number=1N4001 package="300 mil [THT]"]
  Q7 = NPN-Transistor [package="TO92 [THT]"]
  R5 = Resistor [tolerance=±5% resistance=220 package=THT]
  D2 = Rectifier Diode [part_number=1N4001 breakdown_voltage=3.6V package="300 mil [THT]"]
  Q8 = NPN-Transistor [package="TO92 [THT]"]
  R6 = Resistor [tolerance=±5% resistance=220 package=THT]
  Q9 = NPN-Transistor [package="TO92 [THT]"]
  R7 = Resistor [tolerance=±5% resistance=220 package=THT]
  Q10 = NPN-Transistor [package="TO92 [THT]"]
  R8 = Resistor [tolerance=±5% resistance=220 package=THT]
  D5 = Rectifier Diode [part_number=1N4001 package="300 mil [THT]"]
  D6 = Rectifier Diode [part_number=1N4001 package="300 mil [THT]"]
  D8 = Rectifier Diode [part_number=1N4001 package="300 mil [THT]"]
  R9 = Resistor [tolerance=±5% resistance=220 package=THT]
  LED1 = LED - 3mm [color="Red (633nm)" package="3 mm [THT]"]
  D7 = Rectifier Diode [part_number=1N4001 package="300 mil [THT]"]
  R10 = Resistor [tolerance=±5% resistance=220 package=THT]
  LED2 = LED - 3mm [color="Red (633nm)" package="3 mm [THT]"]
  R11 = Resistor [tolerance=±5% resistance=220 package=THT]
  LED3 = LED - 3mm [color="Red (633nm)" package="3 mm [THT]"]
  R12 = Resistor [tolerance=±5% resistance=220 package=THT]
  LED4 = LED - 3mm [color="Red (633nm)" package="3 mm [THT]"]
  R13 = Resistor [tolerance=±5% resistance=220 package=THT]
  LED5 = LED - 3mm [color="Red (633nm)" package="3 mm [THT]"]
  R14 = Resistor [tolerance=±5% resistance=220 package=THT]
  LED6 = LED - 3mm [color="Red (633nm)" package="3 mm [THT]"]
  R15 = Resistor [tolerance=±5% resistance=220 package=THT]
  LED7 = LED - 3mm [color="Red (633nm)" package="3 mm [THT]"]
  R16 = Resistor [tolerance=±5% resistance=220 package=THT]
  LED8 = LED - 3mm [color="Red (633nm)" package="3 mm [THT]"]
  INPUT = screw terminal, 13 pins
  MCP23S1 = MCP23S17 [chip_label=IC package="DIP (Dual Inline) [THT]"]
  LED9 = LED - 3mm [color="Red (633nm)" package="3 mm [THT]"]
  Q11 = NPN-Transistor [package="TO92 [THT]"]
  R17 = Resistor [tolerance=±5% resistance=220 package=THT]
  R18 = Resistor [tolerance=±5% resistance=220 package=THT]
  D9 = Rectifier Diode [part_number=1N4001 package="300 mil [THT]"]
  LED10 = LED - 3mm [color="Red (633nm)" package="3 mm [THT]"]
  Q12 = NPN-Transistor [package="TO92 [THT]"]
  R19 = Resistor [tolerance=±5% resistance=220 package=THT]
  R20 = Resistor [tolerance=±5% resistance=220 package=THT]
  D10 = Rectifier Diode [part_number=1N4001 package="300 mil [THT]"]
  LED11 = LED - 3mm [color="Red (633nm)" package="3 mm [THT]"]
  Q13 = NPN-Transistor [package="TO92 [THT]"]
  R21 = Resistor [tolerance=±5% resistance=220 package=THT]
  R22 = Resistor [tolerance=±5% resistance=220 package=THT]
  D11 = Rectifier Diode [part_number=1N4001 package="300 mil [THT]"]
  LED12 = LED - 3mm [color="Red (633nm)" package="3 mm [THT]"]
  Q14 = NPN-Transistor [package="TO92 [THT]"]
  R23 = Resistor [tolerance=±5% resistance=220 package=THT]
  R24 = Resistor [tolerance=±5% resistance=220 package=THT]
  D12 = Rectifier Diode [part_number=1N4001 package="300 mil [THT]"]
  OUT-RELAY-MODULE-A = male pin header, 7 pins [form="♂ (male)"]
  OUT-RELAY-MODULE-B = male pin header, 7 pins [form="♂ (male)"]
  PWR+OUT-SOCKET-A = screw terminal, 7 pins
  OUT-SOCKET-B = screw terminal, 7 pins

nets:
  N1: RelayController-rev3.D1/TX, INPUT.pin13
  N2: RelayController-rev3.D0/RX, INPUT.pin12
  GND: RelayController-rev3.GND, I2C.pin1, Q3.E, Q4.E, Q5.E, Q6.E, Q7.E, Q8.E, Q9.E, Q10.E, INPUT.pin1, MCP23S1.VSS, MCP23S1.A0, MCP23S1.A1, MCP23S1.A2, Q11.E, Q12.E, Q13.E, Q14.E, OUT-RELAY-MODULE-B.pin1, PWR+OUT-SOCKET-A.pin1
  N3: RelayController-rev3.D2, INPUT.pin11
  N4: RelayController-rev3.D3, INPUT.pin10
  N5: RelayController-rev3.D4, INPUT.pin9
  N6: RelayController-rev3.D5, J16.pin2
  N7: RelayController-rev3.D6, J15.pin2
  N8: RelayController-rev3.D7, INPUT.pin8
  N9: RelayController-rev3.D8, INPUT.pin7
  N10: RelayController-rev3.D9, INPUT.pin6
  N11: RelayController-rev3.D10, MCP23S1.CS
  N12: RelayController-rev3.D11/MOSI, MCP23S1.SI
  N13: RelayController-rev3.D12/MISO, MCP23S1.SO
  5V: RelayController-rev3.5V, D1.cathode, D3.cathode, D4.cathode, D2.cathode, D5.cathode, D6.cathode, D8.cathode, R9.Pin_0, D7.cathode, R10.Pin_0, R11.Pin_0, R12.Pin_0, R13.Pin_0, R14.Pin_0, R15.Pin_0, R16.Pin_0, MCP23S1.VDD, MCP23S1.RESET, R17.Pin_0, D9.cathode, R19.Pin_0, D10.cathode, R21.Pin_0, D11.cathode, R23.Pin_0, D12.cathode, OUT-RELAY-MODULE-A.pin7, PWR+OUT-SOCKET-A.pin2
  N14: RelayController-rev3.A5, I2C.pin2
  N15: RelayController-rev3.A4, I2C.pin3
  N16: RelayController-rev3.A3, INPUT.pin5
  N17: RelayController-rev3.A2, INPUT.pin4
  N18: RelayController-rev3.A1, INPUT.pin2
  N19: RelayController-rev3.A0, INPUT.pin3
  N20: RelayController-rev3.D13/SCK, MCP23S1.SCK
  N21: Q1.gate, J15.pin1
  N22: Q1.drain, DIMMER.pin4
  N23: Q1.source, Q2.source, DIMMER.pin2, DIMMER.pin3
  N24: Q2.gate, J16.pin1
  N25: Q2.drain, DIMMER.pin1
  N26: J15.pin3, R1.Pin_0, OUT-RELAY-MODULE-A.pin6
  N27: J16.pin3, R2.Pin_0, OUT-RELAY-MODULE-A.pin5
  N28: Q3.B, R1.Pin_1
  N29: Q3.C, D1.anode, LED8.cathode, PWR+OUT-SOCKET-A.pin3
  N30: Q4.B, R2.Pin_1
  N31: Q4.C, D2.anode, LED7.cathode, PWR+OUT-SOCKET-A.pin4
  N32: R3.Pin_0, MCP23S1.GPB0, OUT-RELAY-MODULE-A.pin4
  N33: R3.Pin_1, Q5.B
  N34: R4.Pin_0, MCP23S1.GPB1, OUT-RELAY-MODULE-A.pin3
  N35: R4.Pin_1, Q6.B
  N36: Q5.C, D3.anode, LED6.cathode, PWR+OUT-SOCKET-A.pin5
  N37: Q6.C, D4.anode, LED5.cathode, PWR+OUT-SOCKET-A.pin6
  N38: Q7.B, R5.Pin_1
  N39: Q7.C, D5.anode, LED3.cathode, PWR+OUT-SOCKET-A.pin7
  N40: R5.Pin_0, MCP23S1.GPA7, OUT-RELAY-MODULE-A.pin2
  N41: Q8.B, R6.Pin_1
  N42: Q8.C, D6.anode, LED2.cathode, OUT-SOCKET-B.pin1
  N43: R6.Pin_0, MCP23S1.GPA6, OUT-RELAY-MODULE-A.pin1
  N44: Q9.B, R7.Pin_1
  N45: Q9.C, D7.anode, LED4.cathode, OUT-SOCKET-B.pin2
  N46: R7.Pin_0, MCP23S1.GPA5, OUT-RELAY-MODULE-B.pin7
  N47: Q10.B, R8.Pin_1
  N48: Q10.C, D8.anode, LED1.cathode, OUT-SOCKET-B.pin3
  N49: R8.Pin_0, MCP23S1.GPA2, OUT-RELAY-MODULE-B.pin6
  N50: R9.Pin_1, LED1.anode
  N51: R10.Pin_1, LED2.anode
  N52: R11.Pin_1, LED3.anode
  N53: R12.Pin_1, LED4.anode
  N54: R13.Pin_1, LED5.anode
  N55: R14.Pin_1, LED6.anode
  N56: R15.Pin_1, LED7.anode
  N57: R16.Pin_1, LED8.anode
  N58: MCP23S1.GPA0, R20.Pin_0, OUT-RELAY-MODULE-B.pin4
  N59: MCP23S1.GPA1, R18.Pin_0, OUT-RELAY-MODULE-B.pin5
  N60: MCP23S1.GPA3, R22.Pin_0, OUT-RELAY-MODULE-B.pin3
  N61: MCP23S1.GPA4, R24.Pin_0, OUT-RELAY-MODULE-B.pin2
  N62: LED9.cathode, Q11.C, D9.anode, OUT-SOCKET-B.pin4
  N63: LED9.anode, R17.Pin_1
  N64: Q11.B, R18.Pin_1
  N65: LED10.cathode, Q12.C, D10.anode, OUT-SOCKET-B.pin5
  N66: LED10.anode, R19.Pin_1
  N67: Q12.B, R20.Pin_1
  N68: LED11.cathode, Q13.C, D11.anode, OUT-SOCKET-B.pin6
  N69: LED11.anode, R21.Pin_1
  N70: Q13.B, R22.Pin_1
  N71: LED12.cathode, Q14.C, D12.anode, OUT-SOCKET-B.pin7
  N72: LED12.anode, R23.Pin_1
  N73: Q14.B, R24.Pin_1

notes:
  - +
  5V-IN
  OUT-RELAY-A
  1  2  3  4  5
  OUT-RELAY-MODULE-A
  GN-CL-DA
  I2C
  IN
  1  2  3  4  5  6  7  8  9  10 11 12 -
  RELAY-CONTROLLER-3
  DIM|STD
  DIMMER
  D1 - - D2
  6  7  8  9 10 11 12
  OUT-RELAY-B
  OUT-RELAY-MODULE-B
  + 1 2 3 4 5 6 7
  8  9  10 11 12 -
  7     8     9    10    11    12
  1     2     3     4     5     6
  )
  •1
  TX

custom parts:
  MCP23S17: A DIP stand-in part for whatever IC you want. With 28 pins on a 300mil dual inline package (DIP) footprint.
