# Fritzing sketch hc-node-i2c-relay-board (saved by Fritzing 0.9.2b)
circuit board: 3.23934cm x 7.21777cm
breadboards: 1

parts:
  RelayController = Arduino Nano (Rev3.0)
  J1 = shrouded pin header, 10 pins [form="♂ (shrouded male)"]
  J2 = Screw terminal - 2 pins [package=THT]
  J3 = Screw terminal - 2 pins [package=THT]
  J4 = Screw terminal - 2 pins [package=THT]
  J5 = Screw terminal - 2 pins [package=THT]
  J6 = Screw terminal - 2 pins [package=THT]
  J7 = Screw terminal - 2 pins [package=THT]
  J8 = Screw terminal - 2 pins [package=THT]
  J9 = Screw terminal - 2 pins [package=THT]
  + = Screw terminal - 2 pins [package=THT]
  R7 = Resistor [tolerance=±5% resistance=220 package=THT]
  R5 = Resistor [tolerance=±20% resistance=220 package=THT]
  R2 = Resistor [tolerance=±5% resistance=220 package=THT]
  R4 = Resistor [tolerance=±5% resistance=220 package=THT]
  R8 = Resistor [tolerance=±5% resistance=220 package=THT]
  R1 = Resistor [tolerance=±5% resistance=220 package=THT]
  R3 = Resistor [tolerance=±5% resistance=220 package=THT]
  R6 = Resistor [tolerance=±5% resistance=220 package=THT]
  J10 = female pin header, 3 pins [form="♀ (female)"]
  J11 = female pin header, 2 pins [form="♀ (female)"]

nets:
  N1: RelayController.D1/TX, J11.pin2
  N2: RelayController.D0/RX, J11.pin1
  N3: RelayController.GND, J1.pin6, +.pin1, R7.Pin_1, R5.Pin_1, R2.Pin_1, R4.Pin_1, R8.Pin_1, R1.Pin_1, R3.Pin_1, R6.Pin_1, J10.pin3
  N4: RelayController.D2, J1.pin4
  N5: RelayController.D3, J1.pin3
  N6: RelayController.D4, J1.pin2
  N7: RelayController.D5, J9.pin2, R8.Pin_0
  N8: RelayController.D6, J8.pin2, R7.Pin_0
  N9: RelayController.D7, J7.pin2, R6.Pin_0
  N10: RelayController.D8, J6.pin2, R5.Pin_0
  N11: RelayController.D9, J5.pin2, R4.Pin_0
  N12: RelayController.D10, J4.pin2, R3.Pin_0
  N13: RelayController.D11/MOSI, J3.pin2, R1.Pin_0
  N14: RelayController.D12/MISO, J2.pin2, R2.Pin_0
  N15: RelayController.5V, J1.pin1, J2.pin1, J3.pin1, J4.pin1, J5.pin1, J6.pin1, J7.pin1, J8.pin1, J9.pin1, +.pin2
  N16: RelayController.A5, J10.pin2
  N17: RelayController.A4, J10.pin1
  N18: RelayController.A3, J1.pin8
  N19: RelayController.A2, J1.pin7
  N20: RelayController.A1, J1.pin9
  N21: RelayController.A0, J1.pin5
  N22: RelayController.D13/SCK, J1.pin10
