# Fritzing sketch hc-node-i2c-din-relays (saved by Fritzing 0.9.2b)
circuit board: 6.2cm x 8.4cm
breadboards: 1

parts:
  RelayController = Arduino Nano (Rev3.0)
  + = Screw terminal - 2 pins [package=THT]
  J10 = female pin header, 3 pins [form="♀ (female)"]
  Q1 = Basic FET P-Channel [package="TO220 [THT]"]
  Q2 = Basic FET P-Channel [package="TO220 [THT]"]
  J15 = female pin header, 3 pins [form="♀ (female)"]
  J16 = female pin header, 3 pins [form="♀ (female)"]
  J14 = screw terminal, 4 pins
  J1 = male pin header, 10 pins [form="♂ (male)"]
  Q3 = NPN-Transistor [package="TO92 [THT]"]
  R1 = Resistor [tolerance=±5% resistance=10k package=THT]
  D1 = Rectifier Diode [part_number=1N4001 package="300 mil [THT]"]
  Q4 = NPN-Transistor [package="TO92 [THT]"]
  R2 = Resistor [tolerance=±5% resistance=220 package=THT]
  R3 = Resistor [tolerance=±5% resistance=220 package=THT]
  R4 = Resistor [tolerance=±5% resistance=220 package=THT]
  Q5 = NPN-Transistor [package="TO92 [THT]"]
  Q6 = NPN-Transistor [package="TO92 [THT]"]
  D3 = Rectifier Diode [part_number=1N4001 package="300 mil [THT]"]
  D4 = Rectifier Diode [part_number=1N4001 package="300 mil [THT]"]
  Q7 = NPN-Transistor [package="TO92 [THT]"]
  R5 = Resistor [tolerance=±5% resistance=220 package=THT]
  D2 = Rectifier Diode [part_number=1N4001 breakdown_voltage=3.6V package="300 mil [THT]"]
  Q8 = NPN-Transistor [package="TO92 [THT]"]
  R6 = Resistor [tolerance=±5% resistance=220 package=THT]
  Q9 = NPN-Transistor [package="TO92 [THT]"]
  R7 = Resistor [tolerance=±5% resistance=220 package=THT]
  Q10 = NPN-Transistor [package="TO92 [THT]"]
  R8 = Resistor [tolerance=±5% resistance=220 package=THT]
  D5 = Rectifier Diode [part_number=1N4001 package="300 mil [THT]"]
  D6 = Rectifier Diode [part_number=1N4001 package="300 mil [THT]"]
  D8 = Rectifier Diode [part_number=1N4001 package="300 mil [THT]"]
  R9 = Resistor [tolerance=±5% resistance=220 package=THT]
  LED1 = LED - 3mm [color="Red (633nm)" package="3 mm [THT]"]
  D7 = Rectifier Diode [part_number=1N4001 package="300 mil [THT]"]
  R10 = Resistor [tolerance=±5% resistance=220 package=THT]
  LED2 = LED - 3mm [color="Red (633nm)" package="3 mm [THT]"]
  R11 = Resistor [tolerance=±5% resistance=220 package=THT]
  LED3 = LED - 3mm [color="Red (633nm)" package="3 mm [THT]"]
  R12 = Resistor [tolerance=±5% resistance=220 package=THT]
  LED4 = LED - 3mm [color="Red (633nm)" package="3 mm [THT]"]
  R13 = Resistor [tolerance=±5% resistance=220 package=THT]
  LED5 = LED - 3mm [color="Red (633nm)" package="3 mm [THT]"]
  R14 = Resistor [tolerance=±5% resistance=220 package=THT]
  LED6 = LED - 3mm [color="Red (633nm)" package="3 mm [THT]"]
  R15 = Resistor [tolerance=±5% resistance=220 package=THT]
  LED7 = LED - 3mm [color="Red (633nm)" package="3 mm [THT]"]
  R16 = Resistor [tolerance=±5% resistance=220 package=THT]
  LED8 = LED - 3mm [color="Red (633nm)" package="3 mm [THT]"]
  J13 = screw terminal, 9 pins
  J12 = screw terminal, 9 pins

nets:
  N1: RelayController.GND, +.pin1, J10.pin1, J1.pin1, Q3.E, Q4.E, Q5.E, Q6.E, Q7.E, Q8.E, Q9.E, Q10.E, J12.pin1
  N2: RelayController.D2, J1.pin7, R3.Pin_0
  N3: RelayController.D3, J12.pin9
  N4: RelayController.D4, J12.pin8
  N5: RelayController.D5, J12.pin7
  N6: RelayController.D6, J12.pin6
  N7: RelayController.D7, J12.pin5
  N8: RelayController.D8, J12.pin4
  N9: RelayController.D9, J16.pin2
  N10: RelayController.D10, J15.pin2
  N11: RelayController.D11/MOSI, J12.pin3
  N12: RelayController.D12/MISO, J12.pin2
  N13: RelayController.5V, +.pin2, J1.pin10, D1.cathode, D3.cathode, D4.cathode, D2.cathode, D5.cathode, D6.cathode, D8.cathode, R9.Pin_0, D7.cathode, R10.Pin_0, R11.Pin_0, R12.Pin_0, R13.Pin_0, R14.Pin_0, R15.Pin_0, R16.Pin_0, J13.pin1
  N14: RelayController.A5, J10.pin2
  N15: RelayController.A4, J10.pin3
  N16: RelayController.A3, J1.pin6, R4.Pin_0
  N17: RelayController.A2, J1.pin5, R5.Pin_0
  N18: RelayController.A1, J1.pin4, R6.Pin_0
  N19: RelayController.A0, J1.pin3, R7.Pin_0
  N20: RelayController.D13/SCK, J1.pin2, R8.Pin_0
  N21: Q1.gate, J15.pin1
  N22: Q1.drain, J14.pin4
  N23: Q1.source, Q2.source, J14.pin2, J14.pin3
  N24: Q2.gate, J16.pin1
  N25: Q2.drain, J14.pin1
  N26: J15.pin3, J1.pin9, R1.Pin_0
  N27: J16.pin3, J1.pin8, R2.Pin_0
  N28: Q3.B, R1.Pin_1
  N29: Q3.C, D1.anode, LED8.cathode, J13.pin2
  N30: Q4.B, R2.Pin_1
  N31: Q4.C, D2.anode, LED7.cathode, J13.pin3
  N32: R3.Pin_1, Q5.B
  N33: R4.Pin_1, Q6.B
  N34: Q5.C, D3.anode, LED6.cathode, J13.pin4
  N35: Q6.C, D4.anode, LED5.cathode, J13.pin5
  N36: Q7.B, R5.Pin_1
  N37: Q7.C, D5.anode, LED3.cathode, J13.pin6
  N38: Q8.B, R6.Pin_1
  N39: Q8.C, D6.anode, LED2.cathode, J13.pin7
  N40: Q9.B, R7.Pin_1
  N41: Q9.C, D7.anode, LED4.cathode, J13.pin8
  N42: Q10.B, R8.Pin_1
  N43: Q10.C, D8.anode, LED1.cathode, J13.pin9
  N44: R9.Pin_1, LED1.anode
  N45: R10.Pin_1, LED2.anode
  N46: R11.Pin_1, LED3.anode
  N47: R12.Pin_1, LED4.anode
  N48: R13.Pin_1, LED5.anode
  N49: R14.Pin_1, LED6.anode
  N50: R15.Pin_1, LED7.anode
  N51: R16.Pin_1, LED8.anode

notes:
  - +
  5V-IN
  OUTPUT-RELAY
  + 1 2 3 4 5 6 7 8
  1     2     3     4     5     6     7     8
  OUTPUT-RELAY-MODULE
  + 1 2 3 4 5 6 7 8 -
  GND-SCL-SDA
  I2C
  INPUT
  1 2 3 4 5 6 7 8 -
  RELAY-CONTROLLER
  DIM|STD
  DIM1
  DIM2
  TX/RX
